# Fritzing sketch binary_ripple_counter (saved by Fritzing 0.5.2b)
breadboards: 1

parts:
  Arduino1 = Arduino
  IC1 = IC, DIP package, 16 pins [chip_label=74HC4020 spacing=300mil]
  LED1 = Red LED - 5mm [package="5 mm [THT]"]
  LED2 = Red LED - 5mm [package="5 mm [THT]"]
  LED3 = Red LED - 5mm [package="5 mm [THT]"]
  LED4 = Red LED - 5mm [package="5 mm [THT]"]
  LED5 = Red LED - 5mm [package="5 mm [THT]"]
  LED6 = Red LED - 5mm [package="5 mm [THT]"]
  LED7 = Red LED - 5mm [package="5 mm [THT]"]
  LED8 = Red LED - 5mm [package="5 mm [THT]"]
  LED9 = Red LED - 5mm [package="5 mm [THT]"]
  LED10 = Red LED - 5mm [package="5 mm [THT]"]
  R1 = Resistor [resistance=330 package=THT]
  R1_2 = Resistor [resistance=330 package=THT]
  R1_3 = Resistor [resistance=330 package=THT]
  R1_4 = Resistor [resistance=330 package=THT]
  R1_5 = Resistor [resistance=330 package=THT]
  R1_6 = Resistor [resistance=330 package=THT]
  R1_7 = Resistor [resistance=330 package=THT]
  R1_8 = Resistor [resistance=330 package=THT]
  R1_9 = Resistor [resistance=330 package=THT]
  R1_10 = Resistor [resistance=330 package=THT]

nets:
  N1: Arduino1.D4, IC1.pin11
  N2: Arduino1.D3, IC1.pin10
  N3: Arduino1.+5V, IC1.pin16
  N4: Arduino1.GND, IC1.pin8, LED1.cathode, LED2.cathode, LED3.cathode, LED4.cathode, LED5.cathode, LED6.cathode, LED7.cathode, LED8.cathode, LED9.cathode, LED10.cathode
  N5: IC1.pin4, R1_3.Pin_0
  N6: IC1.pin5, R1_5.Pin_0
  N7: IC1.pin6, R1_7.Pin_0
  N8: IC1.pin7, R1_2.Pin_0
  N9: IC1.pin9, R1.Pin_0
  N10: IC1.pin12, R1_10.Pin_0
  N11: IC1.pin13, R1_9.Pin_0
  N12: LED1.anode, R1.Pin_1
  N13: LED2.anode, R1_2.Pin_1
  N14: LED3.anode, R1_3.Pin_1
  N15: LED4.anode, R1_4.Pin_1
  N16: LED5.anode, R1_5.Pin_1
  N17: LED6.anode, R1_6.Pin_1
  N18: LED7.anode, R1_7.Pin_1
  N19: LED8.anode, R1_8.Pin_1
  N20: LED9.anode, R1_9.Pin_1
  N21: LED10.anode, R1_10.Pin_1
